# Fritzing sketch LineBotDiagram (saved by Fritzing 1.0.0d)

parts:
  Part1 = Arduino Nano (Rev3.0)
  M1 = gear-motor
  M2 = gear-motor
  HC-SR04_Sensor_2 = HC-SR04 Ultrasonic Distance Sensor
  LED1 = yf923-f5-f8 [package="8 mm [THT]"]
  LED2 = yf923-f5-f8 [package="8 mm [THT]"]
  LED3 = yf923-f5-f8 [package="8 mm [THT]"]
  LED4 = yf923-f5-f8 [package="8 mm [THT]"]
  X6 = USB Connectors [package=usb-minib]
  U1 = SWITCH_SPDT [package=kps-1290]
  U2 = SWITCH_SPDT [package=kps-1290]
  L298N1 = L298N DC motor driver
  Part3 = FC-03
  Part4 = FC-03
  J1 = Basic Servo

nets:
  GND: Part1.RESET, Part1.GND, HC-SR04_Sensor_2.GND, LED1.Pin_3, LED2.Pin_3, LED3.Pin_3, LED4.Pin_3, X6.D-, X6.GND, L298N1.GND, Part3.GND, Part4.GND, J1.gnd
  N1: Part1.D2, Part3.D0
  N2: Part1.D3, Part4.D0
  N3: Part1.D5, L298N1.IN1
  N4: Part1.D6, L298N1.IN2
  N5: Part1.D7, LED4.Pin_1
  N6: Part1.D9, L298N1.ENB, L298N1.IN4
  N7: Part1.D10, L298N1.IN3
  N8: Part1.D11/MOSI, J1.pulse
  N9: Part1.D12/MISO, HC-SR04_Sensor_2.ECHO
  VCC: Part1.5V, HC-SR04_Sensor_2.VCC, LED1.Pin_2, LED2.Pin_2, LED3.Pin_2, LED4.Pin_2, U1.S, Part3.VCC, Part4.VCC, J1.vcc
  N10: Part1.D13/SCK, HC-SR04_Sensor_2.TRIG
  N11: M1.pin_1, L298N1.OUT1
  N12: M1.pin_2, L298N1.OUT2
  N13: M2.pin_1, L298N1.OUT4
  N14: M2.pin_2, L298N1.OUT3
  N15: LED1.Pin_1, LED2.Pin_4
  N16: LED2.Pin_1, LED3.Pin_4
  N17: LED3.Pin_1, LED4.Pin_4
  N18: X6.VBUS, U1.P, U2.P
  N19: U2.S, L298N1.5V

notes:
  Front ultrasonic sensor
  Gripper servo
  Adressable LEDs
  Movement DC motors
  Rotation encoders
  Motor driver board
  Logic circuit power switch
  Motor circuit power switch
  USB Micro-B power input
  IR Sensor array module

custom parts:
  yf923-f5-f8: F8-LED is a kind of external control constant current integrated lamp bead which integrates high quality single line cascade constant current driver IC and high quality RGB LED chip.
  L298N DC motor driver: 2x DC motor driver with 78M05 positive voltage regulator (7..35 V) L298N: max 46 V, 2 A Set 5 V Enable jumper to enable 5 V regultor (needed for the L298N) and +5 V output at screw terminal or supply external +5 V at screw terminal Set ENA and/or ENB to +5 V to enable motor permanently or supply ENA and/or ENB with PWM signal IN1 and IN2 set rotation directory for motor A (OUT1/OUT2) IN2 and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
  FC-03: FC-03, LM393 IR Speed Sensor Encoder By Nandan
